# Fritzing sketch OttoBotSchem (saved by Fritzing 0.9.3b)
breadboards: 1

parts:
  M1 = DOIT Esp32 DevKit v1 (30 pins long, 11 pins width) [part_number=ESP32S-PIN30]
  J6 = Basic Servo
  J7 = Basic Servo
  J8 = Basic Servo
  J9 = Basic Servo

nets:
  GND: M1.GND, J6.gnd, J7.gnd, J8.gnd, J9.gnd
  N1: M1.D27, J8.pulse
  N2: M1.D14, J7.pulse
  N3: M1.D12, J6.pulse
  N4: M1.D13, J9.pulse
  VCC: M1.VIN, J6.vcc, J7.vcc, J8.vcc, J9.vcc

notes:
  Right leg
  Left Joint
  Left leg
  Right Joint

custom parts:
  DOIT Esp32 DevKit v1 (30 pins long, 11 pins width): The DOIT Esp32 DevKit v1 is one of the development board created by DOIT to evaluate the ESP-WROOM-32 module. It is based on the ESP32 microcontroller that boasts Wifi, Bluetooth, Ethernet and Low Power support all in a single chip. (vanepp) made breadboard work, adjusted pin numbering and labels and reduced size of schematic and cleaned up pcb. This chip is 30pins long (2 x15) and 11 pins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
